// Digital circuit Immediate_Generator.dig as structural Verilog
module Immediate_Generator (
  input  [31:0] instr,
  input  [2:0] \type ,
  output [31:0] imm
);

  Multiplexer #(.Selector_Bits(3), .Bits(32)) multiplexer_1 (
    .sel(\type ), .in_0({{12{instr[31]}}, instr[19:12], instr[20], instr[30:21], 1'b0}),
    .in_1({{21{instr[31]}}, instr[30:20]}), .in_2({{21{instr[31]}}, instr[30:25], instr[11:7]}),
    .in_3({{20{instr[31]}}, instr[7], instr[30:25], instr[11:8], 1'b0}), .in_4({instr[31:12], {12{1'b0}}}),
    .in_5({{12{instr[31]}}, instr[19:12], instr[20], instr[30:21], 1'b0}),
    .in_6({{12{instr[31]}}, instr[19:12], instr[20], instr[30:21], 1'b0}),
    .in_7({{12{instr[31]}}, instr[19:12], instr[20], instr[30:21], 1'b0}), .out(imm));

  // Notes on the sheet:
  //   I-Type
  //   S-Type
  //   B-Type
  //   U-Type
  //   J-Type
endmodule
