// Digital circuit PC_Adder.dig as structural Verilog
module PC_Adder (
  input  [31:0] incr,
  input  [31:0] o_addr,
  output [31:0] n_addr
);

  wire _8bit_adder_1_c_out, _8bit_adder_2_c_out, _8bit_adder_3_c_out;

  _8bit_Adder _8bit_adder_1 (.a(o_addr[7:0]), .b(incr[7:0]), .c_in(1'b0), .s(n_addr[7:0]), .c_out(_8bit_adder_1_c_out));
  _8bit_Adder _8bit_adder_2 (
    .a(o_addr[15:8]), .b(incr[15:8]), .c_in(_8bit_adder_1_c_out), .s(n_addr[15:8]),
    .c_out(_8bit_adder_2_c_out));
  _8bit_Adder _8bit_adder_3 (
    .a(o_addr[23:16]), .b(incr[23:16]), .c_in(_8bit_adder_2_c_out), .s(n_addr[23:16]),
    .c_out(_8bit_adder_3_c_out));
  _8bit_Adder _8bit_adder_4 (
    .a(o_addr[31:24]), .b(incr[31:24]), .c_in(_8bit_adder_3_c_out), .s(n_addr[31:24]));  // open: c_out
endmodule
